# Fritzing sketch Yukari (saved by Fritzing 0.9.3b)
breadboards: 1

parts:
  Pi1 = Adafruit Pi Cobbler
  Part1 = Arduino Nano (Rev3.0)
  IC1 = IC, SIP package, 4 pins [chip_label=MPU9250]  # not connected
  IC2 = IC, SIP package, 6 pins [chip_label=UP501]
  Steering = male pin header, 3 pins [form="♂ (male)"]
  Throttle = male pin header, 4 pins [form="♂ (male)"]
  IC3 = IC, DIP package, 8 pins [chip_label=IC]
  LED1 = LED - 5mm [color="White (4500K)" package="5 mm [THT]"]
  R1 = Resistor [tolerance=±5% resistance=220 package=THT]

nets:
  N1: Pi1.3V3, IC2.pin4, IC2.pin5
  N2: Pi1.SDA0, IC2.pin6
  N3: Pi1.#17, Part1.A3
  N4: Pi1.#21, IC2.pin2
  N5: Pi1.PIN19, Pi1.SCLK, Part1.D0/RX
  N6: Pi1.MOSI, Steering.pin1, Throttle.pin1, R1.Pin_1
  N7: Pi1.MISO, IC3.pin5
  N8: Pi1.PIN25, IC3.pin8, LED1.cathode
  N9: Steering.pin2, Throttle.pin2
  N10: Steering.pin3, IC3.pin7
  N11: Throttle.pin3, IC3.pin6
  N12: LED1.anode, R1.Pin_0

custom parts:
  Adafruit Pi Cobbler: Adafruit Pi Cobbler GPIO Breakout for Raspberry Pi
